# Fritzing sketch remote-circuit (saved by Fritzing 0.9.2b)
breadboards: 1

parts:
  Part1 = Pro Trinket 5V
  U1 = 74HC595 [package="DIP16 [THT]"]
  RIGHT = Momentary Switch [package=ksa_sealed_tac_switch]
  U2 = Voltage Regulator [package=to220-adj]
  LED1 = 7-SEGMENT-4DIGIT-YOUNGSUN [package=7-segment-4digit-youngsun]
  UP = Momentary Switch [package=ksa_sealed_tac_switch]
  DOWN = Momentary Switch [package=ksa_sealed_tac_switch]
  LEFT = Momentary Switch [package=ksa_sealed_tac_switch]
  R1 = Resistor [tolerance=±5% resistance=10k package="0603 [SMD]"]
  R2 = Resistor [tolerance=±5% resistance=10k package="0603 [SMD]"]
  R3 = Resistor [tolerance=±5% resistance=10k package="0603 [SMD]"]
  R4 = Resistor [tolerance=±5% resistance=10k package="0603 [SMD]"]
  R5 = Resistor [tolerance=±5% resistance=220 package="0603 [SMD]"]
  R6 = Resistor [tolerance=±5% resistance=1k package="0603 [SMD]"]
  R7 = Resistor [tolerance=±5% resistance=1.82k package="0805 [SMD]"]
  LED3 = smd LED [color="Infrared (940nm)" package="0603 [SMD]"]

nets:
  GND: Part1.GND, U1.GND, R1.Pin_0, R2.Pin_0, R3.Pin_0, R4.Pin_0, R6.Pin_1, LED3.cathode
  N1: Part1.+5V, RIGHT.4, U2.OUT, UP.4, DOWN.4, LEFT.4
  N2: Part1.D8, LED1.C
  N3: Part1.D6, LED1.APOS-A
  N4: Part1.D5, LED1.DIG2
  N5: Part1.D4, LED1.D
  N6: Part1.D3, LED1.COL-A
  N7: Part1.TXD, LED1.E
  N8: Part1.RXD, LED1.DIG3
  N9: Part1.D9, UP.3, R1.Pin_1
  N10: Part1.D10, DOWN.3, R2.Pin_1
  N11: Part1.D11, LEFT.3, R4.Pin_1
  N12: Part1.D12, RIGHT.3, R3.Pin_1
  N13: Part1.D13, U1.Q3
  N14: Part1.A0, LED1.A
  N15: Part1.A1, U1.Q7'
  N16: Part1.A2, U1.SH_CP
  N17: Part1.A3, U1.DS
  N18: Part1.A4, R5.Pin_0
  N19: U1.Q1, U2.IN, R7.Pin_0
  N20: U1.Q2, LED1.DP
  N21: U1.MR, LED1.F
  N22: U1.ST_CP, LED1.COL-C
  N23: U1.Q0, LED1.G
  N24: U2.ADJ, R6.Pin_0, R7.Pin_1
  N25: R5.Pin_1, LED3.anode

custom parts:
  Pro Trinket 5V: The Pro Trinket 5V is like an Arduino Pro Mini with more pins and USB included. Built with the common core Arduino chip, the ATmega328p, it has 18 GPIO, 2 extra analog inputs, 28K of flash, and 2K of RAM. It has onboard USB bootloading support with Optiboot support, so you can either program your Pro Trinket over USB or with a FTDI cable. The Pro Trinket is programmable using the Arduino IDE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
